// Digital circuit 4-bit adder and subtractor.dig as structural Verilog
module _4_bit_adder_and_subtractor (
  input  B0,
  input  A0,
  input  B1,
  input  A1,
  input  B2,
  input  A2,
  input  B3,
  input  A3,
  input  Subtraction,
  output S0,
  output S1,
  output S2,
  output S3,
  output Co
);

  wire adder_2_co, adder_3_co, adder_4_co, xor_1_out, xor_2_out, xor_3_out, xor_4_out;

  xor xor_1 (xor_1_out, Subtraction, B3);
  adder adder_1 (.A(A3), .Ci(adder_2_co), .B(xor_1_out), .Co(Co), .S(S3));
  xor xor_2 (xor_2_out, Subtraction, B2);
  adder adder_2 (.A(A2), .Ci(adder_3_co), .B(xor_2_out), .Co(adder_2_co), .S(S2));
  xor xor_3 (xor_3_out, Subtraction, B1);
  adder adder_3 (.A(A1), .Ci(adder_4_co), .B(xor_3_out), .Co(adder_3_co), .S(S1));
  xor xor_4 (xor_4_out, Subtraction, B0);
  adder adder_4 (.A(A0), .Ci(Subtraction), .B(xor_4_out), .Co(adder_4_co), .S(S0));
endmodule
