// Digital circuit 4-bit_carry_look_ahead.dig as structural Verilog
module _4_bit_carry_look_ahead (
  input  p0,
  input  g0,
  input  p1,
  input  g1,
  input  p2,
  input  g2,
  input  p3,
  input  g3,
  input  C0,
  output C1,
  output C2,
  output C3,
  output C4
);

  wire and_1_out, and_2_out, and_3_out, and_4_out;

  and and_1 (and_1_out, C0, p0);
  or or_1 (C1, and_1_out, g0);
  and and_2 (and_2_out, C1, p1);
  or or_2 (C2, and_2_out, g1);
  and and_3 (and_3_out, C2, p2);
  or or_3 (C3, and_3_out, g2);
  and and_4 (and_4_out, C3, p3);
  or or_4 (C4, and_4_out, g3);
endmodule
