// Digital circuit 4-bit_carry_look_ahead2.dig as structural Verilog
module _4_bit_carry_look_ahead2 (
  input  p0,
  input  g0,
  input  p1,
  input  g1,
  input  p2,
  input  g2,
  input  p3,
  input  g3,
  input  C0,
  output C1,
  output C2,
  output C3,
  output C4
);

  wire and_1_out, and_2_out, and_3_out, and_4_out, and_5_out, and_6_out, and_7_out, and_8_out, and_9_out,
       and_10_out;

  and and_1 (and_1_out, C0, p0);
  and and_2 (and_2_out, p1, g0);
  and and_3 (and_3_out, p1, p0, C0);
  and and_4 (and_4_out, p2, g1);
  and and_5 (and_5_out, p2, p1, g0);
  and and_6 (and_6_out, p2, p1, p0, C0);
  and and_7 (and_7_out, p3, g2);
  and and_8 (and_8_out, p3, p2, g1);
  and and_9 (and_9_out, p3, p2, p1, g0);
  and and_10 (and_10_out, p3, p2, p1, p0, C0);
  or or_1 (C1, and_1_out, g0);
  or or_2 (C2, and_2_out, and_3_out, g1);
  or or_3 (C3, and_4_out, and_5_out, and_6_out, g2);
  or or_4 (C4, and_7_out, and_8_out, and_9_out, and_10_out, g3);
endmodule
