// Digital circuit adder_for_lookahead.dig as structural Verilog
module adder_for_lookahead (
  input  A,
  input  B,
  input  Ci,
  output P,
  output G,
  output S
);

  xor xor_1 (P, B, A);
  and and_1 (G, B, A);
  xor xor_2 (S, B, A, Ci);
endmodule
