// Digital circuit hw1.dig as structural Verilog
module hw1 (
  input  B2,
  input  A2,
  input  A3,
  input  B3,
  input  SUB,
  input  B0,
  input  A0,
  input  A1,
  input  B1,
  output x,
  output a,
  output b,
  output c,
  output d,
  output e,
  output f,
  output g,
  output g2
);

  wire _4_bit_adder_and_subtractor_1_s0, _4_bit_adder_and_subtractor_1_s1, _4_bit_adder_and_subtractor_1_s2,
       _4_bit_adder_and_subtractor_1_s3;

  _4_bit_adder_and_subtractor _4_bit_adder_and_subtractor_1 (
    .B0(B0), .A0(A0), .B1(B1), .A1(A1), .B2(B2), .A2(A2), .B3(B3), .A3(A3), .Subtraction(SUB),
    .S0(_4_bit_adder_and_subtractor_1_s0), .S1(_4_bit_adder_and_subtractor_1_s1),
    .S2(_4_bit_adder_and_subtractor_1_s2), .S3(_4_bit_adder_and_subtractor_1_s3), .Co(x));
  sub_display sub_display_1 (
    .S3(_4_bit_adder_and_subtractor_1_s3), .S2(_4_bit_adder_and_subtractor_1_s2),
    .S1(_4_bit_adder_and_subtractor_1_s1), .S0(_4_bit_adder_and_subtractor_1_s0), .a(a), .b(b), .c(c), .d(d),
    .e(e), .f(f), .g(g));
  not not_1 (g2, _4_bit_adder_and_subtractor_1_s3);
endmodule
