// Digital circuit test.dig as structural Verilog
module test (
  input  B2,
  input  A2,
  input  A3,
  input  B3,
  input  SUB,
  input  B0,
  input  A0,
  input  A1,
  input  B1,
  input  XX,
  input  XX_2,
  output x
);

  wire _4_bit_adder_and_subtractor_1_s0, _4_bit_adder_and_subtractor_1_s1, _4_bit_adder_and_subtractor_1_s2,
       _4_bit_adder_and_subtractor_1_s3, not_1_out, not_2_out, not_3_out, not_4_out, not_5_out, not_6_out,
       not_7_out;

  _4_bit_adder_and_subtractor _4_bit_adder_and_subtractor_1 (
    .B0(B0), .A0(A0), .B1(B1), .A1(A1), .B2(B2), .A2(A2), .B3(B3), .A3(A3), .Subtraction(SUB),
    .S0(_4_bit_adder_and_subtractor_1_s0), .S1(_4_bit_adder_and_subtractor_1_s1),
    .S2(_4_bit_adder_and_subtractor_1_s2), .S3(_4_bit_adder_and_subtractor_1_s3), .Co(x));
  // sub_display sub_display_1: pin names not known; wires that end beside it: _4_bit_adder_and_subtractor_1_s3, _4_bit_adder_and_subtractor_1_s2, _4_bit_adder_and_subtractor_1_s1, _4_bit_adder_and_subtractor_1_s0
  // Not not_1 has open pins: in=open, out=not_1_out
  // Not not_2 has open pins: in=open, out=not_2_out
  // Not not_3 has open pins: in=open, out=not_3_out
  // Not not_4 has open pins: in=open, out=not_4_out
  // Not not_5 has open pins: in=open, out=not_5_out
  // Not not_6 has open pins: in=open, out=not_6_out
  // Not not_7 has open pins: in=open, out=not_7_out
  Seven_Seg seven_seg_1 (
    .a(XX_2), .b(XX_2), .c(XX_2), .d(XX_2), .e(XX_2), .f(XX_2), .g(_4_bit_adder_and_subtractor_1_s3),
    .dp(XX_2));
  Seven_Seg seven_seg_2 (
    .a(not_1_out), .b(not_2_out), .c(not_3_out), .d(not_4_out), .e(not_5_out), .f(not_6_out), .g(not_7_out),
    .dp(XX));
endmodule
