// Digital circuit test2.dig as structural Verilog
module test2 (
  input  A3,
  input  B3,
  input  A2,
  input  B2,
  input  A1,
  input  B1,
  input  A0,
  input  B0,
  input  C0,
  output S0,
  output S1,
  output S2,
  output S3,
  output C4,
  output S0_2,
  output S1_2,
  output S2_2,
  output S3_2,
  output C4_2
);

  wire _4_bit_carry_look_ahead2_1_c1, _4_bit_carry_look_ahead2_1_c2, _4_bit_carry_look_ahead2_1_c3, adder0_g,
       adder0_p, adder1_g, adder1_p, adder2_g, adder2_p, adder3_g, adder3_p, adder_1_co, adder_2_co,
       adder_3_co;

  adder adder_1 (.A(A0), .Ci(C0), .B(B0), .Co(adder_1_co), .S(S0_2));
  adder adder_2 (.A(A1), .Ci(adder_1_co), .B(B1), .Co(adder_2_co), .S(S1_2));
  adder adder_3 (.A(A2), .Ci(adder_2_co), .B(B2), .Co(adder_3_co), .S(S2_2));
  adder adder_4 (.A(A3), .Ci(adder_3_co), .B(B3), .Co(C4_2), .S(S3_2));
  adder_for_lookahead adder0 (.A(A0), .B(B0), .Ci(C0), .P(adder0_p), .G(adder0_g), .S(S0));
  adder_for_lookahead adder1 (.A(A1), .B(B1), .Ci(_4_bit_carry_look_ahead2_1_c1), .P(adder1_p), .G(adder1_g), .S(S1));
  adder_for_lookahead adder2 (.A(A2), .B(B2), .Ci(_4_bit_carry_look_ahead2_1_c2), .P(adder2_p), .G(adder2_g), .S(S2));
  adder_for_lookahead adder3 (.A(A3), .B(B3), .Ci(_4_bit_carry_look_ahead2_1_c3), .P(adder3_p), .G(adder3_g), .S(S3));
  _4_bit_carry_look_ahead2 _4_bit_carry_look_ahead2_1 (
    .p0(adder0_p), .g0(adder0_g), .p1(adder1_p), .g1(adder1_g), .p2(adder2_p), .g2(adder2_g), .p3(adder3_p),
    .g3(adder3_g), .C0(C0), .C1(_4_bit_carry_look_ahead2_1_c1), .C2(_4_bit_carry_look_ahead2_1_c2),
    .C3(_4_bit_carry_look_ahead2_1_c3), .C4(C4));
endmodule
