// Digital circuit hw1-1.dig as structural Verilog
module hw1_1 (
  input  A3,
  input  A2,
  input  A1,
  input  A0,
  output F3,
  output F2,
  output F1,
  output F0
);

  wire nand_1_out, nand_2_out, nand_3_out, nand_4_out, nand_5_out, nand_6_out, nand_7_out, nand_8_out,
       nand_9_out, nand_10_out, nand_11_out, nand_12_out, nand_13_out, not_1_out, not_2_out, not_3_out,
       not_4_out;

  not not_1 (not_1_out, A3);
  not not_2 (not_2_out, A2);
  not not_3 (not_3_out, A1);
  not not_4 (not_4_out, A0);
  nand nand_1 (nand_1_out, not_1_out, A2, A1);
  nand nand_2 (nand_2_out, A3, not_2_out, not_3_out);
  nand nand_3 (nand_3_out, not_1_out, not_2_out, A1, A0);
  nand nand_4 (nand_4_out, not_1_out, A2, not_3_out);
  nand nand_5 (nand_5_out, A3, not_2_out, not_3_out, A0);
  nand nand_6 (nand_6_out, not_1_out, not_2_out, A1, not_4_out);
  nand nand_7 (nand_7_out, not_1_out, A2, not_3_out, A0);
  nand nand_8 (nand_8_out, A3, not_2_out, not_3_out, not_4_out);
  nand nand_9 (nand_9_out, not_1_out, not_3_out, A0);
  nand nand_10 (nand_10_out, not_1_out, not_2_out, A1, not_4_out);
  nand nand_11 (nand_11_out, not_1_out, A2, not_3_out);
  nand nand_12 (nand_12_out, not_1_out, A2, A0);
  nand nand_13 (nand_13_out, A3, not_2_out, not_3_out, not_4_out);
  nand nand_14 (F3, nand_1_out, nand_2_out);
  nand nand_15 (F2, nand_3_out, nand_4_out, nand_5_out);
  nand nand_16 (F1, nand_6_out, nand_7_out, nand_8_out);
  nand nand_17 (F0, nand_9_out, nand_10_out, nand_11_out, nand_12_out, nand_13_out);
endmodule
