// Digital circuit hw1-2.dig as structural Verilog
module hw1_2 (
  input  A0,
  input  A1,
  input  A2,
  input  A3,
  output F3,
  output F2,
  output F1,
  output F0
);

  wire decoder_1_out_0, decoder_1_out_1, decoder_1_out_2, decoder_1_out_3, decoder_1_out_4, decoder_1_out_5,
       decoder_1_out_6, decoder_1_out_7, decoder_1_out_8, decoder_1_out_9, decoder_1_out_10,
       decoder_1_out_11, decoder_1_out_12, decoder_1_out_13, decoder_1_out_14, decoder_1_out_15;

  Decoder #(.Selector_Bits(4)) decoder_1 (
    .sel({A3, A2, A1, A0}), .out_0(decoder_1_out_0), .out_1(decoder_1_out_1), .out_2(decoder_1_out_2),
    .out_3(decoder_1_out_3), .out_4(decoder_1_out_4), .out_5(decoder_1_out_5), .out_6(decoder_1_out_6),
    .out_7(decoder_1_out_7), .out_8(decoder_1_out_8), .out_9(decoder_1_out_9), .out_10(decoder_1_out_10),
    .out_11(decoder_1_out_11), .out_12(decoder_1_out_12), .out_13(decoder_1_out_13),
    .out_14(decoder_1_out_14), .out_15(decoder_1_out_15));
  or or_1 (F3, decoder_1_out_9, decoder_1_out_8, decoder_1_out_7, decoder_1_out_6);
  or or_2 (F2, decoder_1_out_9, decoder_1_out_5, decoder_1_out_4, decoder_1_out_3);
  or or_3 (F1, decoder_1_out_8, decoder_1_out_5, decoder_1_out_2);
  or or_4 (F0, decoder_1_out_8, decoder_1_out_7, decoder_1_out_5, decoder_1_out_4, decoder_1_out_2, decoder_1_out_1);
endmodule
