// Digital circuit hw21.dig as structural Verilog
module hw21 (
  input  Xi,
  input  Yi,
  input  Ci0,
  input  Ci1,
  output Co0,
  output Co1
);

  wire nand_1_out, nand_2_out, nand_3_out, nand_4_out, nand_5_out, nand_6_out, not_1_out, not_2_out,
       not_3_out, not_4_out;

  not not_1 (not_1_out, Xi);
  not not_2 (not_2_out, Yi);
  not not_3 (not_3_out, Ci0);
  not not_4 (not_4_out, Ci1);
  nand nand_1 (nand_1_out, not_3_out, Ci1, not_1_out);
  nand nand_2 (nand_2_out, not_3_out, Ci1, Yi);
  nand nand_3 (nand_3_out, not_1_out, Yi);
  nand nand_4 (nand_4_out, Ci0, not_4_out, not_2_out);
  nand nand_5 (nand_5_out, Ci0, not_4_out, Xi);
  nand nand_6 (nand_6_out, Xi, not_2_out);
  nand nand_7 (Co1, nand_1_out, nand_2_out, nand_3_out);
  nand nand_8 (Co0, nand_4_out, nand_5_out, nand_6_out);
endmodule
