// Digital circuit hw22.dig as structural Verilog
module hw22 (
  input  Ci1,
  input  Ci0,
  input  Yi,
  input  Xi,
  output Co0,
  output Co1
);

  wire decoder_1_out_0, decoder_1_out_1, decoder_1_out_2, decoder_1_out_3, decoder_1_out_4, decoder_1_out_5,
       decoder_1_out_6, decoder_1_out_7, decoder_1_out_8, decoder_1_out_9, decoder_1_out_10,
       decoder_1_out_11, decoder_1_out_12, decoder_1_out_13, decoder_1_out_14, decoder_1_out_15;

  Decoder #(.Selector_Bits(4)) decoder_1 (
    .sel({Xi, Yi, Ci0, Ci1}), .out_0(decoder_1_out_0), .out_1(decoder_1_out_1), .out_2(decoder_1_out_2),
    .out_3(decoder_1_out_3), .out_4(decoder_1_out_4), .out_5(decoder_1_out_5), .out_6(decoder_1_out_6),
    .out_7(decoder_1_out_7), .out_8(decoder_1_out_8), .out_9(decoder_1_out_9), .out_10(decoder_1_out_10),
    .out_11(decoder_1_out_11), .out_12(decoder_1_out_12), .out_13(decoder_1_out_13),
    .out_14(decoder_1_out_14), .out_15(decoder_1_out_15));
  or or_1 (Co0, decoder_1_out_14, decoder_1_out_11, decoder_1_out_10, decoder_1_out_9, decoder_1_out_8, decoder_1_out_2);
  or or_2 (Co1, decoder_1_out_13, decoder_1_out_7, decoder_1_out_6, decoder_1_out_5, decoder_1_out_4, decoder_1_out_1);
endmodule
