// Digital circuit test2.dig as structural Verilog
module test2 (
  input  X0,
  input  Y0,
  input  X1,
  input  Y1,
  input  X2,
  input  Y2,
  input  X3,
  input  Y3,
  output X,
  output Y
);

  wire hw21_1_co0, hw21_1_co1, hw21_2_co0, hw21_2_co1, hw21_3_co0, hw21_3_co1;

  hw21 hw21_1 (.Xi(X0), .Yi(Y0), .Ci0(1'b0), .Ci1(1'b0), .Co0(hw21_1_co0), .Co1(hw21_1_co1));
  hw21 hw21_2 (.Xi(X1), .Yi(Y1), .Ci0(hw21_1_co0), .Ci1(hw21_1_co1), .Co0(hw21_2_co0), .Co1(hw21_2_co1));
  hw21 hw21_3 (.Xi(X2), .Yi(Y2), .Ci0(hw21_2_co0), .Ci1(hw21_2_co1), .Co0(hw21_3_co0), .Co1(hw21_3_co1));
  hw21 hw21_4 (.Xi(X3), .Yi(Y3), .Ci0(hw21_3_co0), .Ci1(hw21_3_co1), .Co0(X), .Co1(Y));
endmodule
