// Digital circuit adder_and_subtractor.dig as structural Verilog
module adder_and_subtractor (
  input  A0,
  input  B0,
  input  Sub,
  input  A1,
  input  B1,
  input  A2,
  input  B2,
  input  A3,
  input  B3,
  output S0,
  output S1,
  output S2,
  output S3,
  output Cout
);

  wire u_adder_and_subtractor_2_cout, u_adder_and_subtractor_3_cout, u_adder_and_subtractor_4_cout;

  adder_and_subtractor #(.applicationType("GHDL")) u_adder_and_subtractor (
    .X(A3), .Y(B3), .Cin(u_adder_and_subtractor_2_cout), .sub(Sub), .Sum(S3), .Cout(Cout));
  adder_and_subtractor #(.applicationType("GHDL")) u_adder_and_subtractor_2 (
    .X(A2), .Y(B2), .Cin(u_adder_and_subtractor_3_cout), .sub(Sub), .Sum(S2),
    .Cout(u_adder_and_subtractor_2_cout));
  adder_and_subtractor #(.applicationType("GHDL")) u_adder_and_subtractor_3 (
    .X(A1), .Y(B1), .Cin(u_adder_and_subtractor_4_cout), .sub(Sub), .Sum(S1),
    .Cout(u_adder_and_subtractor_3_cout));
  adder_and_subtractor #(.applicationType("GHDL")) u_adder_and_subtractor_4 (
    .X(A0), .Y(B0), .Cin(1'b0), .sub(Sub), .Sum(S0), .Cout(u_adder_and_subtractor_4_cout));
endmodule

/* Code of adder_and_subtractor:
LIBRARY ieee;
USE ieee.std_logic_1164.all;
USE ieee.numeric_std.all;

entity adder_and_subtractor is
  port (
    X, Y, Cin, sub: in std_logic;
    Sum, Cout: out std_logic);
end adder_and_subtractor;

architecture Equations of adder_and_subtractor is
begin
	-- concurrent assignment statements
	cout  <= (y and cin) or (x and y and not sub) or(x and cin and not sub) or (not x and y and sub) or (not x and cin and sub);
	sum <= (not x and not y and cin) or (not x and y and not cin) or (x and y and cin) or (x and not y and not cin);
end Equations;
*/
