// Digital circuit sub display decoder.dig as structural Verilog
module sub_display_decoder (
  input  S3,
  input  S2,
  input  S1,
  input  S0,
  input  SUB,
  output a,
  output b,
  output c,
  output d,
  output e,
  output f,
  output g
);

  wire and_1_out, and_2_out, and_3_out, and_4_out, and_5_out, and_6_out, and_7_out, and_8_out, and_9_out,
       and_10_out, and_11_out, and_12_out, and_13_out, and_14_out, and_15_out, and_16_out, and_17_out,
       and_18_out, and_19_out, and_20_out, and_21_out, and_22_out, and_23_out, and_24_out, and_25_out,
       and_26_out, not_1_out, not_2_out, not_3_out, not_4_out, or_1_out, or_2_out, or_3_out, or_4_out,
       or_5_out, seven_segment_display_decoder_1_p5, seven_segment_display_decoder_1_p6,
       seven_segment_display_decoder_1_p7, seven_segment_display_decoder_1_p8,
       seven_segment_display_decoder_1_p9, seven_segment_display_decoder_1_p10,
       seven_segment_display_decoder_1_p11;

  not not_1 (not_1_out, S3);
  not not_2 (not_2_out, S2);
  not not_3 (not_3_out, S1);
  not not_4 (not_4_out, S0);
  and and_1 (and_1_out, not_4_out, not_3_out, S2);
  and and_2 (and_2_out, S0, S1, S2);
  and and_3 (and_3_out, S1, not_2_out);
  and and_4 (and_4_out, not_4_out, S1, S2);
  and and_5 (and_5_out, S0, not_3_out, not_2_out);
  and and_6 (and_6_out, not_4_out, not_3_out, S2);
  and and_7 (and_7_out, S0, S1, S2);
  and and_8 (and_8_out, not_3_out, S2);
  and and_9 (and_9_out, S0, S2);
  and and_10 (and_10_out, S1, S2);
  and and_11 (and_11_out, S0, not_3_out, not_2_out);
  and and_12 (and_12_out, S0, S1, S2);
  // seven_segment_display_decoder seven_segment_display_decoder_1: pin names not known; wires that end beside it: S3, S2, S1, S0, seven_segment_display_decoder_1_p5, seven_segment_display_decoder_1_p6, seven_segment_display_decoder_1_p7, seven_segment_display_decoder_1_p8, seven_segment_display_decoder_1_p9, seven_segment_display_decoder_1_p10, seven_segment_display_decoder_1_p11
  or or_1 (or_1_out, and_1_out, and_2_out);
  or or_2 (or_2_out, and_5_out, and_6_out, and_7_out);
  or or_3 (or_3_out, S0, and_8_out);
  or or_4 (or_4_out, and_9_out, and_10_out);
  or or_5 (or_5_out, and_11_out, and_12_out);
  and and_13 (and_13_out, not_1_out, SUB, seven_segment_display_decoder_1_p5);
  and and_14 (and_14_out, not_1_out, SUB, seven_segment_display_decoder_1_p6);
  and and_15 (and_15_out, not_1_out, SUB, seven_segment_display_decoder_1_p7);
  and and_16 (and_16_out, not_1_out, SUB, seven_segment_display_decoder_1_p8);
  and and_17 (and_17_out, not_1_out, SUB, seven_segment_display_decoder_1_p9);
  and and_18 (and_18_out, not_1_out, SUB, seven_segment_display_decoder_1_p10);
  and and_19 (and_19_out, not_1_out, SUB, seven_segment_display_decoder_1_p11);
  and and_20 (and_20_out, or_1_out, S3, SUB);
  and and_21 (and_21_out, and_3_out, S3, SUB);
  and and_22 (and_22_out, and_4_out, S3, SUB);
  and and_23 (and_23_out, or_2_out, S3, SUB);
  and and_24 (and_24_out, or_3_out, S3, SUB);
  and and_25 (and_25_out, or_4_out, S3, SUB);
  and and_26 (and_26_out, or_5_out, S3, SUB);
  or or_6 (a, and_13_out, and_20_out);
  or or_7 (b, and_14_out, and_21_out);
  or or_8 (c, and_15_out, and_22_out);
  or or_9 (d, and_16_out, and_23_out);
  or or_10 (e, and_17_out, and_24_out);
  or or_11 (f, and_18_out, and_25_out);
  or or_12 (g, and_19_out, and_26_out);
endmodule
