// Digital circuit sub display.dig as structural Verilog
module sub_display (
  input  S3,
  input  S2,
  input  S1,
  input  S0,
  output a,
  output b,
  output c,
  output d,
  output e,
  output f,
  output g
);

  wire and_1_out, and_2_out, and_3_out, and_4_out, and_5_out, and_6_out, and_7_out, and_8_out, and_9_out,
       and_10_out, and_11_out, and_12_out, and_13_out, and_14_out, and_15_out, and_16_out, and_17_out,
       and_18_out, and_19_out, and_20_out, not_1_out, not_2_out, not_3_out, not_4_out;

  not not_1 (not_1_out, S3);
  not not_2 (not_2_out, S2);
  not not_3 (not_3_out, S1);
  not not_4 (not_4_out, S0);
  and and_1 (and_1_out, S0, not_3_out, not_2_out, not_1_out);
  and and_2 (and_2_out, not_4_out, not_3_out, S2);
  and and_3 (and_3_out, S0, S1, S2, S3);
  and and_4 (and_4_out, S0, not_3_out, S2, not_1_out);
  and and_5 (and_5_out, not_4_out, S1, S2, not_1_out);
  and and_6 (and_6_out, S1, not_2_out, S3);
  and and_7 (and_7_out, not_4_out, S1, not_2_out, not_1_out);
  and and_8 (and_8_out, not_4_out, S1, S2, S3);
  and and_9 (and_9_out, S0, not_3_out, not_2_out);
  and and_10 (and_10_out, not_4_out, not_3_out, S2);
  and and_11 (and_11_out, S0, S1, S2);
  and and_12 (and_12_out, not_3_out, S2);
  and and_13 (and_13_out, S0, not_2_out, not_1_out);
  and and_14 (and_14_out, S0, S2, S3);
  and and_15 (and_15_out, S0, S1, S2);
  and and_16 (and_16_out, S1, not_2_out, not_1_out);
  and and_17 (and_17_out, S1, S2, S3);
  and and_18 (and_18_out, S0, S1, S2);
  and and_19 (and_19_out, S0, not_3_out, not_2_out);
  and and_20 (and_20_out, not_3_out, not_2_out, not_1_out);
  or or_1 (a, and_1_out, and_2_out, and_3_out);
  or or_2 (b, and_4_out, and_5_out, and_6_out);
  or or_3 (c, and_7_out, and_8_out);
  or or_4 (d, and_9_out, and_10_out, and_11_out);
  or or_5 (e, S0, and_12_out);
  or or_6 (g, and_18_out, and_19_out, and_20_out);
  or or_7 (f, and_13_out, and_14_out, and_15_out, and_16_out, and_17_out);
endmodule
