// Digital circuit test.dig as structural Verilog
module test (
  input  B2,
  input  A2,
  input  A3,
  input  B3,
  input  SUB,
  input  B0,
  input  A0,
  input  A1,
  input  B1,
  input  XX,
  input  XX_2,
  output x
);

  wire not_1_out, not_2_out, not_3_out, not_4_out, not_5_out, not_6_out, not_7_out, undriven;

  // Not not_1 has open pins: in=open, out=not_1_out
  // Not not_2 has open pins: in=open, out=not_2_out
  // Not not_3 has open pins: in=open, out=not_3_out
  // Not not_4 has open pins: in=open, out=not_4_out
  // Not not_5 has open pins: in=open, out=not_5_out
  // Not not_6 has open pins: in=open, out=not_6_out
  // Not not_7 has open pins: in=open, out=not_7_out
  Seven_Seg seven_seg_1 (.a(XX_2), .b(XX_2), .c(XX_2), .d(XX_2), .e(XX_2), .f(XX_2), .g(undriven), .dp(XX_2));
  Seven_Seg seven_seg_2 (
    .a(not_1_out), .b(not_2_out), .c(not_3_out), .d(not_4_out), .e(not_5_out), .f(not_6_out), .g(not_7_out),
    .dp(XX));
endmodule
