// Digital circuit comparator4.dig as structural Verilog
module comparator4 (
  input  [3:0] X,
  input  [3:0] Y,
  input  Ci0,
  input  CI1,
  output X_2,
  output Y_2
);

  Comparator4 #(.applicationType("GHDL")) u_Comparator4 (.X(X), .Y(Y), .Ci0(Ci0), .Ci1(CI1), .Co0(X_2), .Co1(Y_2));
endmodule

/* Code of Comparator4:
LIBRARY ieee;
USE ieee.std_logic_1164.all;
USE ieee.numeric_std.all;

entity Comparator4 is
port (
    X, Y: in std_logic_vector(3 downto 0);
    Ci0, Ci1: in std_logic;
    Co0, Co1: out std_logic);
end Comparator4;

architecture Structure of Comparator4 is
component Comparator
	port (Xi, Yi, Ci0, Ci1: in std_logic;
	     Co0, Co1: out std_logic);
end component;

signal C1: std_logic_vector(2 downto 0);
signal C2: std_logic_vector(2 downto 0);
begin
	CP0: Comparator port map(X(0), Y(0), Ci0, Ci1, C1(0), C2(0));
	CP1: Comparator port map(X(1), Y(1), C1(0), C2(0), C1(1), C2(1));
	CP2: Comparator port map(X(2), Y(2), C1(1), C2(1), C1(2), C2(2));
	CP3: Comparator port map(X(3), Y(3), C1(2), C2(2), Co0, Co1);
end Structure;

LIBRARY ieee;
USE ieee.std_logic_1164.all;
USE ieee.numeric_std.all;

entity Comparator is
  port (
    Xi, Yi, Ci0, Ci1: in std_logic;
    Co0, Co1: out std_logic);
end Comparator;

architecture Equations of Comparator is
    signal input: std_logic_vector (0 to 3);
begin
    input <= Xi & Yi & Ci0 & Ci1;
    with input select
    Co0 <= '1' when "0010",
	   '1' when "1000",
	   '1' when "1001",
	   '1' when "1010",
	   '1' when "1011",
	   '1' when "1110",
	   '0' when others;
    with input select
    Co1 <= '1' when "0001",
	   '1' when "0100",
	   '1' when "0101",
	   '1' when "0110",
	   '1' when "0111",
	   '1' when "1101",
	   '0' when others;

end Equations;
*/
