// Digital circuit S-R_flip-flap.dig as structural Verilog
module S_R_flip_flap (
  input  S,
  input  R,
  input  bottom,
  output Q,
  output QN
);

  wire and_1_out, and_2_out, and_3_out, and_4_out, not_1_out, s_r_latch_1_p, s_r_latch_1_q;

  not not_1 (not_1_out, bottom);
  and and_1 (and_1_out, S, not_1_out);
  and and_2 (and_2_out, not_1_out, R);
  S_R_Latch s_r_latch_1 (.S(and_1_out), .R(and_2_out), .P(s_r_latch_1_p), .Q(s_r_latch_1_q));
  and and_3 (and_3_out, s_r_latch_1_p, bottom);
  and and_4 (and_4_out, s_r_latch_1_q, bottom);
  S_R_Latch s_r_latch_2 (.S(and_3_out), .R(and_4_out), .P(Q), .Q(QN));
endmodule
