// Digital circuit S-R_flip-flap_VHDLdig.dig as structural Verilog
module S_R_flip_flap_VHDLdig (
  input  S,
  input  R,
  input  CLK,
  output Q,
  output Q_2
);

  SRFF #(.applicationType("GHDL")) u_SRFF (.S(S), .R(R), .CLK(CLK), .Q(Q_2), .QN(Q));

  // Notes on the sheet:
  //   CLK: Hz: 2
endmodule

/* Code of SRFF:
LIBRARY ieee;
USE ieee.std_logic_1164.all;
USE ieee.numeric_std.all;

entity SRFF is
port (S, R, CLK: in std_logic;
      Q, QN: out std_logic);	
end SRFF;

architecture SRFF1 of SRFF is
signal Qint: std_logic;
begin
	Q <= Qint;	
	QN <= not Qint;	
	process (CLK)	
	begin
		if clk'event and clk = '1' then
			Qint <= S or (not R and Qint);
		end if;
	 end process;
end SRFF1;
*/
