// Digital circuit HW2-1.dig as structural Verilog
module HW2_1 (
  input  in_1,
  input  clk,
  input  SUB,
  input  [1:0] in_5,
  input  in_6,
  input  in_7,
  input  in_8,
  input  [3:0] in_9,
  input  in_10,
  input  in_11,
  input  in_12,
  input  XX,
  input  XX_2,
  output Co
);

  wire not_1_out, not_2_out, not_3_out, not_4_out, not_5_out, not_6_out, not_7_out;
  wire [3:0] _4_bit_adder_and_subtractor_1_s0, demultiplexer_1_out_0, demultiplexer_1_out_1,
       multiplexer_1_out, register_1_q, register_2_q, u_my_SRAM_do;

  Demultiplexer #(.Bits(4)) demultiplexer_1 (
    .sel(in_1), .in(u_my_SRAM_do), .out_0(demultiplexer_1_out_0), .out_1(demultiplexer_1_out_1));
  Register #(.Bits(4)) register_1 (.D(demultiplexer_1_out_0), .C(clk), .en(in_11), .Q(register_1_q));
  test #(.applicationType("GHDL")) u_test ();  // open: clk, x, a_out, b_out, c_out, d_out, e_out
  _4_bit_adder_and_subtractor _4_bit_adder_and_subtractor_1 (
    .B0(register_1_q[0]), .A0(demultiplexer_1_out_1[0]), .B1(register_1_q[1]), .A1(demultiplexer_1_out_1[1]),
    .B2(register_1_q[2]), .A2(demultiplexer_1_out_1[2]), .B3(register_1_q[3]), .A3(demultiplexer_1_out_1[3]),
    .Subtraction(SUB), .S0(_4_bit_adder_and_subtractor_1_s0[0]), .S1(_4_bit_adder_and_subtractor_1_s0[1]),
    .S2(_4_bit_adder_and_subtractor_1_s0[2]), .S3(_4_bit_adder_and_subtractor_1_s0[3]), .Co(Co));
  Register #(.Bits(4)) register_2 (.D(_4_bit_adder_and_subtractor_1_s0), .C(clk), .en(in_12), .Q(register_2_q));
  // sub_display sub_display_1: pin names not known; wires that end beside it: register_2_q[3], register_2_q[2], register_2_q[1], register_2_q[0]
  // Not not_1 has open pins: in=open, out=not_1_out
  // Not not_2 has open pins: in=open, out=not_2_out
  // Not not_3 has open pins: in=open, out=not_3_out
  // Not not_4 has open pins: in=open, out=not_4_out
  // Not not_5 has open pins: in=open, out=not_5_out
  // Not not_6 has open pins: in=open, out=not_6_out
  // Not not_7 has open pins: in=open, out=not_7_out
  Multiplexer #(.Bits(4)) multiplexer_1 (.sel(in_10), .in_0(in_9), .in_1(register_2_q), .out(multiplexer_1_out));
  Seven_Seg seven_seg_1 (.a(XX_2), .b(XX_2), .c(XX_2), .d(XX_2), .e(XX_2), .f(XX_2), .g(register_2_q[3]), .dp(XX_2));
  Seven_Seg seven_seg_2 (
    .a(not_1_out), .b(not_2_out), .c(not_3_out), .d(not_4_out), .e(not_5_out), .f(not_6_out), .g(not_7_out),
    .dp(XX));
  my_SRAM #(.applicationType("GHDL")) u_my_SRAM (
    .D(multiplexer_1_out), .Address(in_5), .ChipSelect(in_6), .WE(in_7), .OE(in_8), .DO(u_my_SRAM_do));

  // Notes on the sheet:
  //   clk: Hz: 10
endmodule

/* Code of test:
LIBRARY ieee;
USE ieee.std_logic_1164.all;
USE ieee.numeric_std.all;

entity test is	
	port	(
		-- Input ports
		clk, x: in  std_logic;
		
		-- Output ports		
		a_out, b_out, c_out, d_out: out std_logic;
		e_out: out std_logic_vector(3 downto 0));
end test;

architecture state_graph of test is	
	signal z : std_logic_vector(7 downto 0) := "00000000";
	signal f : std_logic_vector(2 downto 0) := "000";
Begin
	
	z <= a_out & b_out & c_out & d_out & e_out;
	with f select
	z <= "00000000" when "000",
	     "00000110" when "001",
	     "00001110" when "010",
	     "01000101" when "011",
	     "10111101" when "100",
	     "10111111" when "101",
	     "00000000" when others;
	
	process(clk) is
 	begin
 		if(rising_edge(clk)) then
			if(f = "000" and x = '1') then f <= "001";
			elsif(f = "001" and x = '1') then f <= "010";
			elsif(f = "010" and x = '1') then f <= "011";
			elsif(f = "011" and x = '1') then f <= "100";
			elsif(f = "100" and x = '1') then f <= "101";
			elsif(f = "101" and x = '1') then f <= "100";
			elsif (x = '0') then f <= "000";
			end if;
		end if;
	end process; 
end state_graph;
*/

/* Code of my_SRAM:
LIBRARY ieee;
USE ieee.std_logic_1164.all;
USE ieee.numeric_std.all;

entity my_SRAM is
port (	D: in std_logic_vector(3 downto 0);
	Address: in std_logic_vector(1 downto 0);
	ChipSelect, WE, OE: in std_logic;
	DO: out std_logic_vector(3 downto 0));
end my_SRAM;

architecture SRAM_simple of my_SRAM is

type memory is array (0 to 3) of std_logic_vector(3 downto 0);
signal SRAM_internal: memory := ("0000", "0000","0000","0000");
signal Address_int: integer;
signal Address_temp: std_logic_vector(1 downto 0);

begin
	
	Address_int <= to_integer(unsigned(Address));

	DO <= "ZZZZ" when ChipSelect = '0'
	else "ZZZZ" when OE = '0'
	else SRAM_internal(Address_int) when OE = '1';
	
	SRAM_internal(Address_int) <= D when WE = '1';

end SRAM_simple;
*/
