// Digital circuit HW2.dig as structural Verilog
module HW2 (
  input  S1,
  input  SUB,
  input  [1:0] Add,
  input  WE,
  input  OE,
  input  [3:0] Data,
  input  S0,
  input  EN1,
  input  EN2,
  input  CLK,
  output Co,
  output S3,
  output a,
  output b,
  output c,
  output d,
  output e,
  output f,
  output g
);

  wire [3:0] _4_bit_adder_and_subtractor_1_s0, demultiplexer_1_out_0, demultiplexer_1_out_1,
       multiplexer_1_out, register_1_q, register_2_q, u_my_SRAM_do;

  Demultiplexer #(.Bits(4)) demultiplexer_1 (
    .sel(S1), .in(u_my_SRAM_do), .out_0(demultiplexer_1_out_0), .out_1(demultiplexer_1_out_1));
  Register #(.Bits(4)) register_1 (.D(demultiplexer_1_out_0), .C(CLK), .en(EN1), .Q(register_1_q));
  _4_bit_adder_and_subtractor _4_bit_adder_and_subtractor_1 (
    .B0(register_1_q[0]), .A0(demultiplexer_1_out_1[0]), .B1(register_1_q[1]), .A1(demultiplexer_1_out_1[1]),
    .B2(register_1_q[2]), .A2(demultiplexer_1_out_1[2]), .B3(register_1_q[3]), .A3(demultiplexer_1_out_1[3]),
    .Subtraction(SUB), .S0(_4_bit_adder_and_subtractor_1_s0[0]), .S1(_4_bit_adder_and_subtractor_1_s0[1]),
    .S2(_4_bit_adder_and_subtractor_1_s0[2]), .S3(_4_bit_adder_and_subtractor_1_s0[3]), .Co(Co));
  Register #(.Bits(4)) register_2 (.D(_4_bit_adder_and_subtractor_1_s0), .C(CLK), .en(EN2), .Q(register_2_q));
  sub_display sub_display_1 (
    .S3(register_2_q[3]), .S2(register_2_q[2]), .S1(register_2_q[1]), .S0(register_2_q[0]), .a(a), .b(b),
    .c(c), .d(d), .e(e), .f(f), .g(g));
  not not_1 (S3, register_2_q[3]);
  Multiplexer #(.Bits(4)) multiplexer_1 (.sel(S0), .in_0(Data), .in_1(register_2_q), .out(multiplexer_1_out));
  my_SRAM #(.applicationType("GHDL")) u_my_SRAM (
    .D(multiplexer_1_out), .Address(Add), .ChipSelect(1'b1), .WE(WE), .OE(OE), .DO(u_my_SRAM_do));
endmodule

/* Code of my_SRAM:
LIBRARY ieee;
USE ieee.std_logic_1164.all;
USE ieee.numeric_std.all;

entity my_SRAM is
port (	D: in std_logic_vector(3 downto 0);
	Address: in std_logic_vector(1 downto 0);
	ChipSelect, WE, OE: in std_logic;
	DO: out std_logic_vector(3 downto 0));
end my_SRAM;

architecture SRAM_simple of my_SRAM is

type memory is array (0 to 3) of std_logic_vector(3 downto 0);
signal SRAM_internal: memory := ("0000", "0000","0000","0000");
signal Address_int: integer;
signal Address_temp: std_logic_vector(1 downto 0);

begin
	
	Address_int <= to_integer(unsigned(Address));

	DO <= "ZZZZ" when ChipSelect = '0'
	else "ZZZZ" when OE = '0'
	else SRAM_internal(Address_int) when OE = '1';
	
	SRAM_internal(Address_int) <= D when WE = '1';

end SRAM_simple;
*/
