// Digital circuit adder.dig as structural Verilog
module adder (
  input  A,
  input  Ci,
  input  B,
  output Co,
  output S
);

  wire and_1_out, and_2_out, and_3_out;

  xor xor_1 (S, A, B, Ci);
  and and_1 (and_1_out, A, B);
  and and_2 (and_2_out, A, Ci);
  and and_3 (and_3_out, B, Ci);
  or or_1 (Co, and_1_out, and_2_out, and_3_out);
endmodule
