// Digital circuit HW2-2.dig as structural Verilog
module HW2_2 (
  input  clk,
  input  clk_2,
  output a,
  output b,
  output c,
  output C_2,
  output B_2,
  output A_2
);

  wire A_nq, and_1_out, and_2_out, and_3_out, and_4_out, and_5_out, B_nq, C_nq, or_1_out, or_2_out, or_3_out;

  test #(.applicationType("GHDL")) u_test (.clk(clk), .a_out(a), .b_out(b), .c_out(c));
  and and_1 (and_1_out, C_2, C_nq);
  and and_2 (and_2_out, B_nq, C_nq);
  and and_3 (and_3_out, B_2, A_2);
  and and_4 (and_4_out, A_nq, B_nq);
  and and_5 (and_5_out, C_2, B_2);
  or or_1 (or_1_out, and_1_out, A_nq);
  or or_2 (or_2_out, and_2_out, and_3_out);
  or or_3 (or_3_out, and_4_out, and_5_out);
  JK_FF u_A (.J(B_nq), .C(clk_2), .K(or_2_out), .Q(C_2), .nQ(A_nq));
  JK_FF u_B (.J(or_1_out), .C(clk_2), .K(1'b1), .Q(B_2), .nQ(B_nq));
  JK_FF u_C (.J(or_3_out), .C(clk_2), .K(B_nq), .Q(A_2), .nQ(C_nq));
endmodule

/* Code of test:
library ieee;
use ieee.std_logic_1164.all;
entity test is	
	port	(
		-- Input ports
		clk	: in  std_logic;
		
		-- Output ports		
		a_out, b_out, c_out	: out std_logic	);
end test;

architecture state_graph of test is	
	signal z : std_logic_vector(2 downto 0) := "000";
Begin
	a_out <= z(0);
	b_out <= z(1);
	c_out <= z(2);
	process(clk) is
 	begin
 		if(rising_edge(clk)) then
			if(z = "000") then z <= "111";
			elsif(z = "001") then z <= "110";
			elsif(z = "010") then z <= "000";
			elsif(z = "100") then z <= "010";
			elsif(z = "101") then z <= "100";
			elsif(z = "110") then z <= "101";
			elsif(z = "111") then z <= "001";
                        else z <= "000";
 			end if;
		end if;
	end process; 
end state_graph;
*/
