// Digital circuit HW2.dig as structural Verilog
module HW2 (
  input  clk,
  input  x,
  output a,
  output b,
  output c,
  output z
);

  test #(.applicationType("GHDL")) u_test (.clk(clk), .x(x), .a_out(a), .b_out(b), .c_out(c), .f(z));
endmodule

/* Code of test:
library ieee;
use ieee.std_logic_1164.all;

entity test is	
	port	(
		-- Input ports
		clk, x: in  std_logic;
		
		-- Output ports		
		a_out, b_out, c_out, f: out std_logic	);
end test;


architecture test_boolean_arch of test is	
	signal Ta, Tb, Tc : std_logic;	
	signal a, b, c : std_logic := '0';
begin	
	f <= (a and x) or (b and not c and x);
	a_out <= a;
	b_out <= b;
	c_out <= c;
	Ta <= a or (b and not x and c);
	Tb <= c or (b and not x) or (a and not x) or (not a and not b and x);
	Tc <= b or not x or (not a and not c);
	
	process(clk) is 
 	begin
 		if(rising_edge(clk)) then
			a <= Ta xor a;
			b <= Tb xor b;
			c <= Tc xor c;
		end if;
	end process;
 end test_boolean_arch;
*/
