// Digital circuit HW2.dig as structural Verilog
module HW2 (
  input  clk,
  input  SUB,
  input  [3:0] in_4,
  input  XX,
  input  XX_2,
  input  in_7,
  output Co
);

  wire not_1_out, not_2_out, not_3_out, not_4_out, not_5_out, not_6_out, not_7_out, u_control_circuit_a_out,
       u_control_circuit_b_out, u_control_circuit_c_out, u_control_circuit_d_out;
  wire [1:0] u_control_circuit_e_out_2;
  wire [2:0] u_control_circuit_e_out;
  wire [3:0] _4_bit_adder_and_subtractor_1_s0, demultiplexer_1_out_0, demultiplexer_1_out_1,
       multiplexer_1_out, register_1_q, register_2_q, u_my_SRAM_do;

  Demultiplexer #(.Bits(4)) demultiplexer_1 (
    .sel(u_control_circuit_a_out), .in(u_my_SRAM_do), .out_0(demultiplexer_1_out_0),
    .out_1(demultiplexer_1_out_1));
  Register #(.Bits(4)) register_1 (.D(demultiplexer_1_out_0), .C(clk), .en(u_control_circuit_b_out), .Q(register_1_q));
  _4_bit_adder_and_subtractor _4_bit_adder_and_subtractor_1 (
    .B0(register_1_q[0]), .A0(demultiplexer_1_out_1[0]), .B1(register_1_q[1]), .A1(demultiplexer_1_out_1[1]),
    .B2(register_1_q[2]), .A2(demultiplexer_1_out_1[2]), .B3(register_1_q[3]), .A3(demultiplexer_1_out_1[3]),
    .Subtraction(SUB), .S0(_4_bit_adder_and_subtractor_1_s0[0]), .S1(_4_bit_adder_and_subtractor_1_s0[1]),
    .S2(_4_bit_adder_and_subtractor_1_s0[2]), .S3(_4_bit_adder_and_subtractor_1_s0[3]), .Co(Co));
  control_circuit #(.applicationType("GHDL")) u_control_circuit (
    .clk(clk), .x(in_7), .a_out(u_control_circuit_a_out), .b_out(u_control_circuit_b_out),
    .c_out(u_control_circuit_c_out), .d_out(u_control_circuit_d_out),
    .e_out({u_control_circuit_e_out_2, u_control_circuit_e_out}));
  Register #(.Bits(4)) register_2 (
    .D(_4_bit_adder_and_subtractor_1_s0), .C(clk), .en(u_control_circuit_c_out), .Q(register_2_q));
  // sub_display sub_display_1: pin names not known; wires that end beside it: register_2_q[3], register_2_q[2], register_2_q[1], register_2_q[0]
  // Not not_1 has open pins: in=open, out=not_1_out
  // Not not_2 has open pins: in=open, out=not_2_out
  // Not not_3 has open pins: in=open, out=not_3_out
  // Not not_4 has open pins: in=open, out=not_4_out
  // Not not_5 has open pins: in=open, out=not_5_out
  // Not not_6 has open pins: in=open, out=not_6_out
  // Not not_7 has open pins: in=open, out=not_7_out
  Multiplexer #(.Bits(4)) multiplexer_1 (
    .sel(u_control_circuit_d_out), .in_0(in_4), .in_1(register_2_q), .out(multiplexer_1_out));
  Seven_Seg seven_seg_1 (.a(XX_2), .b(XX_2), .c(XX_2), .d(XX_2), .e(XX_2), .f(XX_2), .g(register_2_q[3]), .dp(XX_2));
  Seven_Seg seven_seg_2 (
    .a(not_1_out), .b(not_2_out), .c(not_3_out), .d(not_4_out), .e(not_5_out), .f(not_6_out), .g(not_7_out),
    .dp(XX));
  my_SRAM #(.applicationType("GHDL")) u_my_SRAM (
    .D(multiplexer_1_out), .Address(u_control_circuit_e_out_2), .ChipSelect(u_control_circuit_e_out[2]),
    .WE(u_control_circuit_e_out[1]), .OE(u_control_circuit_e_out[0]), .DO(u_my_SRAM_do));

  // Notes on the sheet:
  //   clk: Hz: 10
endmodule

/* Code of control_circuit:
LIBRARY ieee;
USE ieee.std_logic_1164.all;
USE ieee.numeric_std.all;

entity control_circuit is	
	port	(
		clk, x: in  std_logic;
		a_out, b_out, c_out, d_out: out std_logic;
		e_out: out std_logic_vector(4 downto 0));
end control_circuit;

architecture boolean of control_circuit is	
	signal z : std_logic_vector(0 to 8) := "000000000";
	signal f : std_logic_vector(2 downto 0);
	signal a, b, c : std_logic := '0';
	signal Ta, Tb, Tc : std_logic;
Begin
	f <= a & b & c;

	a_out <= z(0);
	b_out <= z(1);
	c_out <= z(2);
	d_out <= z(3);
	e_out <= z(4 to 8);

	z <= 	"000000000" when f = "000" else
		"000000110" when f = "001" else
		"000001110" when f = "010" else
		"010000101" when f = "011" else
		"101101101" when f = "100" else
		"101101111" when f = "101";

	Ta <= (a and not x) or (b and c and x);
	Tb <= (b and not x) or (b and c) or (not a and c and x);
	Tc <= x or c;
	
	process(clk) is
 	begin
 		if(rising_edge(clk)) then
			a <= Ta xor a;
			b <= Tb xor b;
			c <= Tc xor c;
		end if;
	end process; 
end boolean;
*/

/* Code of my_SRAM:
LIBRARY ieee;
USE ieee.std_logic_1164.all;
USE ieee.numeric_std.all;

entity my_SRAM is
port (	D: in std_logic_vector(3 downto 0);
	Address: in std_logic_vector(1 downto 0);
	ChipSelect, WE, OE: in std_logic;
	DO: out std_logic_vector(3 downto 0));
end my_SRAM;

architecture SRAM_simple of my_SRAM is

type memory is array (0 to 3) of std_logic_vector(3 downto 0);
signal SRAM_internal: memory := ("0000", "0000","0000","0000");
signal Address_int: integer;
signal Address_temp: std_logic_vector(1 downto 0);

begin
	
	Address_int <= to_integer(unsigned(Address));

	DO <= "ZZZZ" when ChipSelect = '0'
	else "ZZZZ" when OE = '0'
	else SRAM_internal(Address_int) when OE = '1';
	
	SRAM_internal(Address_int) <= D when WE = '1';

end SRAM_simple;
*/
